# Fritzing sketch EmergencyLights_groundfill_order (saved by Fritzing 1.0.2b)
circuit board: 10.5cm x 8.5cm
breadboards: 1

parts:
  out = female pin header, 5 pins [form="♀ (female)"]
  in = female pin header, 5 pins [form="♀ (female)"]
  Fuse_2A = Fuse with Handler [part_number=Htc-15m]
  +_- = screw terminal, 2 pins
  -_B1_+ = male pin header, 2 pins [form="♂ (male)"]
  strip_1 = male pin header, 2 pins [form="♂ (male)"]
  strip_2 = male pin header, 2 pins [form="♂ (male)"]
  strip_3 = male pin header, 2 pins [form="♂ (male)"]
  strip_4 = male pin header, 2 pins [form="♂ (male)"]
  emcy_1 = male pin header, 2 pins [form="♂ (male)"]
  emcy_2 = male pin header, 2 pins [form="♂ (male)"]
  -_in_+ = female pin header, 6 pins [form="♀ (female)"]
  -_out_+ = female pin header, 6 pins [form="♀ (female)"]
  D1 = DIODE-SCHOTTKY [package=sma-diode]
  Buck_CC_CV_-_8s_11_2V_-_10s_14V_-_0_2C = Pad [width=6 height=5 connect=center]  # not connected
  PS_18V = Pad [width=6 height=5 connect=center]  # not connected
  Emergency_Light_rev_1 = Pad [width=4 height=4 connect=center]  # not connected
  J1_9V = Pad [width=4 height=4 connect=center]  # not connected
  Fuse_0_5A = Fuse with Handler [part_number=Htc-15m]
  -_B2_+ = male pin header, 2 pins [form="♂ (male)"]

nets (from the schematic view):
  N1: out.pin1, in.pin1, +_-.pin1, strip_2.pin2, strip_4.pin2, emcy_1.pin2, emcy_2.pin2, -_in_+.pin6
  N2: out.pin5, emcy_1.pin1, emcy_2.pin1
  N3: in.pin5, D1.C, Fuse_0_5A.Connector2
  N4: Fuse_2A.Connector1, +_-.pin2
  N5: Fuse_2A.Connector2, strip_1.pin1, strip_3.pin1, -_in_+.pin1
  N6: -_B1_+.pin1, -_out_+.pin6
  N7: -_B1_+.pin2, -_B2_+.pin1
  N8: strip_1.pin2, strip_2.pin1
  N9: strip_3.pin2, strip_4.pin1
  N10: -_out_+.pin1, D1.A
  N11: Fuse_0_5A.Connector1, -_B2_+.pin2
